// Logisim project ChooseFunction.circ as structural Verilog: 1 circuit, main circuit main
module main (
  input  x,
  input  y,
  input  z
);

  wire and_1_out, and_2_out, not_1_out, xor_1_out;

  not not_1 (not_1_out, x);
  and and_1 (and_1_out, x, y);
  and and_2 (and_2_out, not_1_out, z);
  xor xor_1 (xor_1_out, and_1_out, and_2_out);
  // Probe on xor_1_out

  // Notes on the sheet:
  //   w1
  //   w2
  //   w3
endmodule
