// Logisim project MajorityFunction.circ as structural Verilog: 1 circuit, main circuit main
module main (
  input  x,
  input  y,
  input  z
);

  wire and_1_out, and_2_out, and_3_out, xor_1_out, xor_2_out;

  and and_1 (and_1_out, x, y);
  and and_2 (and_2_out, z, x);
  and and_3 (and_3_out, y, z);
  xor xor_1 (xor_1_out, and_1_out, and_2_out);
  xor xor_2 (xor_2_out, xor_1_out, and_3_out);
  // Probe on xor_2_out

  // Notes on the sheet:
  //   w1
  //   w2
  //   w3
  //   w4
endmodule
